# Fritzing sketch dd_cap_optocoupler (saved by Fritzing 0.9.4)

parts:
  Part1 = Arduino Nano (Rev3.0)
  R2 = Resistor [tolerance=±5% resistance=1M package=THT]
  R3 = Resistor [tolerance=±5% resistance=1M package=THT]
  R4 = Resistor [tolerance=±5% resistance=1M package=THT]
  J1 = Camdenboss CTB0158-4 [part_number=CTB0158-4 package=THT]
  R5 = Resistor [tolerance=±5% resistance=1M package=THT]
  J3 = Camdenboss CTB0158-2 [part_number=CTB0158-2 package=THT]
  D1 = Diode [package=diode-1n4148]
  D2 = Rectifier Diode 10A [part_number=P1000K]
  U1 = Sharp PC817 [package=THT]
  J4 = Camdenboss CTB0158-2 [part_number=CTB0158-2 package=THT]

nets:
  N1: Part1.GND, D1.A, U1.Pin_2
  N2: Part1.D2, J1.pin4, R5.Pin_1
  N3: Part1.D3, R5.Pin_0
  N4: Part1.D4, R3.Pin_1, J1.pin3
  N5: Part1.D5, R3.Pin_0
  N6: Part1.D6, R4.Pin_1, J1.pin2
  N7: Part1.D7, R4.Pin_0
  N8: Part1.D8, R2.Pin_1, J1.pin1
  N9: Part1.D9, R2.Pin_0
  N10: Part1.D12/MISO, U1.Pin_1
  N11: Part1.5V, J3.pin2
  N12: J3.pin1, D1.C
  N13: D2.cathode, U1.Pin_4
  N14: D2.anode, J4.pin1
  N15: U1.Pin_3, J4.pin2
