# Fritzing sketch dd_cap_relay (saved by Fritzing 0.9.4)

parts:
  Part1 = Arduino Nano (Rev3.0)
  R2 = Resistor [tolerance=±5% resistance=1M package=THT]
  R3 = Resistor [tolerance=±5% resistance=1M package=THT]
  R4 = Resistor [tolerance=±5% resistance=1M package=THT]
  J1 = Camdenboss CTB0158-4 [part_number=CTB0158-4 package=THT]
  R5 = Resistor [tolerance=±5% resistance=1M package=THT]
  OMRON1 = OMRON PCB Power Relay – G5LE [part_number="G5LE-1\n" package=THT]
  J2 = Camdenboss CTB0158-3 [part_number=CTB0158-3 package=THT]
  J3 = Camdenboss CTB0158-2 [part_number=CTB0158-2 package=THT]
  D1 = Diode [package=diode-1n4148]

nets:
  N1: Part1.GND, OMRON1.COIL1, D1.A
  N2: Part1.D2, J1.pin4, R5.Pin_1
  N3: Part1.D3, R3.Pin_1, J1.pin3
  N4: Part1.D4, R4.Pin_1, J1.pin2
  N5: Part1.D5, R2.Pin_1, J1.pin1
  N6: Part1.D6, R5.Pin_0
  N7: Part1.D7, R3.Pin_0
  N8: Part1.D8, R4.Pin_0
  N9: Part1.D9, R2.Pin_0
  N10: Part1.D12/MISO, OMRON1.COIL2
  N11: Part1.5V, J3.pin2
  N12: OMRON1.A, J2.pin3
  N13: OMRON1.C, J2.pin2
  N14: OMRON1.B, J2.pin1
  N15: J3.pin1, D1.C
