# Fritzing sketch dd_cap_MPR121 (saved by Fritzing 0.9.4)

parts:
  Part1 = Arduino Nano (Rev3.0)
  Part2 = MPR121 Breakout

nets:
  GND: Part1.GND, Part2.GND
  N1: Part1.A5, Part2.SCL
  N2: Part1.A4, Part2.SDA
  3V3: Part1.3V3, Part2.3.3V
